# Fritzing sketch SmartHomeCoreX (saved by Fritzing 0.9.5d)

parts:
  U1 = ESP32-38PinWide [part_number=ESP32-38PinWide]
  KY-1 = Keyes Relay [package=THT]
  KY-2 = Keyes Relay [package=THT]
  KY-3 = Keyes Relay [package=THT]
  KY-4 = Keyes Relay [package=THT]
  DHT1 = DHT11 Humitidy and Temperature Sensor
  J1 = 2.1mm Barrel Jack with Terminal Block

nets:
  N1: U1.3.3, DHT1.VDD
  N2: U1.GPIO2, KY-1.power
  N3: U1.GPIO0, KY-2.power
  N4: U1.GPIO4, DHT1.DATA
  N5: U1.GPIO16, KY-3.power
  N6: U1.GPIO17, KY-4.power
  GND: U1.GND, DHT1.GND
  N7: KY-1.signal, KY-2.signal, KY-3.signal, KY-4.signal
  N8: KY-1.ground, KY-2.ground, KY-3.ground, KY-4.ground, J1.NEG

custom parts:
  ESP32-38PinWide: Generic 38-Pin ESP32 with wide format (only access to one side of pins on a breadboard) based on Stephen Lilley's HiLetgo ESP-WROOM-32 ESP32 ESP-32S Development Board.
  Keyes Relay: The Keyes 5V relay module is suitable for SCM development, home appliance control. It uses a 5V~12V TIL control signal which can control DC / AC signal.
  DHT11 Humitidy and Temperature Sensor: DHT11 Humidity and Temperature Sensor
